# Fritzing sketch arduino-bluetooth (saved by Fritzing 0.9.3b)
breadboards: 1

parts:
  Part1 = Bluetooth HC-05 Macho
  R1 = Resistor [tolerance=±5% resistance=1k package=THT]
  Part2 = Arduino Uno (Rev3)
  R2 = Resistor [tolerance=±5% resistance=2k package=THT]

nets:
  N1: Part1.TXD, Part2.D2
  N2: Part1.RXD, R1.Pin_0
  VCC: Part1.VCC, Part2.5V
  GND: Part1.GND, Part2.GND, R2.Pin_1
  N3: R1.Pin_1, Part2.D3_PWM, R2.Pin_0
